# Fritzing sketch layout (saved by Fritzing 0.9.3b)
breadboards: 1

parts:
  Arduino = Arduino Uno (Rev3)
  Avoid_Sensor = fc-51 [package=THT]
  Display_Matrix = LED Matrix - Serial Interface - Red/Green/Blue

nets:
  N1: Arduino.D3_PWM, Avoid_Sensor.pin1
  N2: Arduino.D4, Display_Matrix.MOSI
  N3: Arduino.D5_PWM, Display_Matrix.CS
  N4: Arduino.D6_PWM, Display_Matrix.SCK
  5V: Arduino.5V, Avoid_Sensor.pin3, Display_Matrix.VCC
  GND: Arduino.GND, Avoid_Sensor.pin2, Display_Matrix.GND
